# Fritzing sketch WriteToDAC (saved by Fritzing 0.9.2b)
breadboards: 1

parts:
  J1 = T Cobbler Plus
  Raspberry_Pi1 = Raspberry Pi 2
  U1 = MCP4725 [package=SOT23-6]
  U3 = 7-SEGMENT-DISPLAY [package=7-segment-display]
  U4 = 74HC595 [package="DIP16 [THT]"]
  U5 = 74HC595 [package="DIP16 [THT]"]
  ON = LED - 5mm [color="Red (633nm)" package="5 mm [THT]"]
  R1 = Resistor [tolerance=±5% resistance=220 package=THT]
  S1 = Pushbutton [package="[THT]"]
  U2 = 7-SEGMENT-DISPLAY [package=7-segment-display]
  R4 = Resistor [tolerance=±5% resistance=220 package=THT]
  R3 = Resistor [tolerance=±5% resistance=220 package=THT]

nets (from the schematic view):
  5V: J1.5.0V#1, U1.VDD
  N1: J1.SDA, U1.SDA
  N2: J1.SCL, U1.SCL
  GND: J1.GND#5, U1.VSS, U1.AO, U4.GND, U5.GND, R4.Pin_0, R3.Pin_0
  N3: J1.#17, U5.DS
  N4: J1.#18, U4.OE, U5.OE
  N5: J1.#27, U4.SH_CP, U4.ST_CP, U5.SH_CP, U5.ST_CP
  3.3V: J1.3.3V#16, U4.MR, U4.VCC, U5.MR, U5.VCC, ON.anode
  N6: J1.#24, R1.Pin_1
  N7: J1.GND#19, S1.Pin_3, S1.Pin_4
  N8: J1.#25, S1.Pin_1, S1.Pin_2
  3V3: J1.3.3V#41, J1.3.3V#57, Raspberry_Pi1.3v3, Raspberry_Pi1.3V3
  5V_2: J1.5V, Raspberry_Pi1.5V
  N9: J1.GPIO_2, Raspberry_Pi1.GPIO2
  N10: J1.GPIO_3, Raspberry_Pi1.GPIO3
  N11: J1.GND#46, J1.GND#49, J1.GND#54, J1.GND#60, J1.GND#65, J1.GND#70, J1.GND#74, J1.GND#79, Raspberry_Pi1.GND
  N12: J1.GPIO_4, Raspberry_Pi1.GPIO4
  N13: J1.GPIO_14, Raspberry_Pi1.GPIO14
  N14: J1.GPIO_15, Raspberry_Pi1.GPIO15
  N15: J1.GPIO_17, Raspberry_Pi1.GPIO17
  N16: J1.GPIO_18, Raspberry_Pi1.GPIO18
  N17: J1.GPIO_27, Raspberry_Pi1.GPIO27
  N18: J1.GPIO_22, Raspberry_Pi1.GPIO22
  N19: J1.GPIO_23, Raspberry_Pi1.GPIO23
  N20: J1.GPIO_24, Raspberry_Pi1.GPIO24
  N21: J1.GPIO_10, Raspberry_Pi1.GPIO10
  N22: J1.GPIO_9, Raspberry_Pi1.GPIO9
  N23: J1.GPIO_25, Raspberry_Pi1.GPIO25
  N24: J1.GPIO_11, Raspberry_Pi1.GPIO11
  N25: J1.GPIO_8, Raspberry_Pi1.GPIO8
  N26: J1.GPIO_7, Raspberry_Pi1.GPIO7
  N27: J1.ID_SD, Raspberry_Pi1.ID_SD
  N28: J1.ID_SC, Raspberry_Pi1.ID_SC
  N29: J1.GPIO_5, Raspberry_Pi1.GPIO5
  N30: J1.GPIO_6, Raspberry_Pi1.GPIO6
  N31: J1.GPIO_12, Raspberry_Pi1.GPIO12
  N32: J1.GPIO_13, Raspberry_Pi1.GPIO13
  N33: J1.GPIO_19, Raspberry_Pi1.GPIO19
  N34: J1.GPIO_16, Raspberry_Pi1.GPIO16
  N35: J1.GPIO_26, Raspberry_Pi1.GPIO26
  N36: J1.GPIO_20, Raspberry_Pi1.GPIO20
  N37: J1.GPIO_21, Raspberry_Pi1.GPIO21
  DAC OUT: U1.VOUT
  N38: U3.E, U5.Q4
  N39: U3.D, U5.Q3
  N40: U3.C, U5.Q2
  N41: U3.DP, U5.Q7
  N42: U3.B, U5.Q1
  N43: U3.A, U5.Q0
  N44: U3.G2, R4.Pin_1
  N45: U3.F, U5.Q5
  N46: U3.G, U5.Q6
  N47: U4.Q1, U2.B
  N48: U4.Q2, U2.C
  N49: U4.Q3, U2.D
  N50: U4.Q4, U2.E
  N51: U4.Q5, U2.F
  N52: U4.Q6, U2.G
  N53: U4.Q7, U2.DP
  N54: U4.DS, U5.Q7'
  N55: U4.Q0, U2.A
  N56: ON.cathode, R1.Pin_0
  N57: U2.G1, U2.G2, R3.Pin_1

custom parts:
  T Cobbler Plus: The T-Cobbler Plus is an add on prototyping board from Adafruit specifically designed for the Raspberry Pi B+ that can break out all those tasty power, GPIO, I2C and SPI pins from the 40-pin header onto a solderless breadboard. This set will make "cobbling together" prototypes with the Pi super easy. The T-Cobbler Plus can plug into any solderless breadboard.
