# Fritzing sketch Displays_ADC_DAC_LED_test (saved by Fritzing 0.9.1b)
breadboards: 2

parts:
  J1 = T Cobbler Plus
  U1 = 74HC595 [package="DIP16 [THT]"]
  DAC1 = MCP4725 12-bit DAC Breakout
  U2 = 74HC595 [package="DIP16 [THT]"]
  IC1 = MCP3008 8-channel 10-bit ADC [part_number=MCP3008]
  7SEG1 = 7-Segment LED I2C Backpack (red)
  R1 = Resistor [tolerance=±5% resistance=180 package=THT]
  LED1 = LED - 5mm [color="Green (570nm)" package="5 mm [THT]"]
  LED2 = LED - 5mm [color="Red (633nm)" package="5 mm [THT]"]
  R2 = Resistor [tolerance=±5% resistance=10k package=THT]
  7_Segment5 = 7 Segment Display
  R3 = Resistor [tolerance=±5% resistance=180 package=THT]
  R4 = Resistor [tolerance=±5% resistance=180 package=THT]
  R5 = Resistor [tolerance=±5% resistance=180 package=THT]
  R6 = Resistor [tolerance=±5% resistance=180 package=THT]
  R7 = Resistor [tolerance=±5% resistance=180 package=THT]
  R8 = Resistor [tolerance=±5% resistance=180 package=THT]
  R9 = Resistor [tolerance=±5% resistance=180 package=THT]
  R10 = Resistor [tolerance=±5% resistance=180 package=THT]
  7_Segment6 = 7 Segment Display
  R11 = Resistor [tolerance=±5% resistance=180 package=THT]
  R12 = Resistor [tolerance=±5% resistance=180 package=THT]
  R13 = Resistor [tolerance=±5% resistance=180 package=THT]
  R14 = Resistor [tolerance=±5% resistance=180 package=THT]
  R15 = Resistor [tolerance=±5% resistance=180 package=THT]
  R16 = Resistor [tolerance=±5% resistance=180 package=THT]
  R17 = Resistor [tolerance=±5% resistance=180 package=THT]
  R18 = Resistor [tolerance=±5% resistance=180 package=THT]

nets:
  VCC: J1.3V3, U1.MR, U1.VCC, U2.MR, U2.VCC
  N1: J1.SDA, DAC1.SCL, 7SEG1.SCL
  N2: J1.SCL, DAC1.SDA, 7SEG1.SDA
  GND: J1.GND#5, U1.GND, U2.GND
  N3: J1.#4, U1.SH_CP, U2.SH_CP
  N4: J1.TXD, U2.DS
  N5: J1.RXD, U2.ST_CP
  N6: J1.#17, U1.DS
  N7: J1.#18, U1.ST_CP
  3.3V: J1.3.3V, DAC1.VDD, IC1.no_name_yet#1, IC1.no_name_yet#15, IC1.no_name_yet#16, 7SEG1.V+, R1.Pin_0, R2.Pin_0
  N8: J1.MOSI, IC1.no_name_yet#11
  GND_2: J1.GND#19, DAC1.GND, 7SEG1.GND
  N9: J1.MISO, IC1.no_name_yet#12
  N10: J1.SCLK, IC1.no_name_yet#13
  N11: J1.CE0, IC1.no_name_yet#10
  N12: J1.#5, DAC1.A0
  N13: J1.#19, U1.OE
  N14: J1.#16, U2.OE
  N15: J1.GND#38, IC1.no_name_yet#4, IC1.no_name_yet#5, IC1.no_name_yet#6, IC1.no_name_yet#7, IC1.no_name_yet#9, IC1.no_name_yet#14, LED1.cathode, LED2.cathode
  N16: U1.Q1, R11.Pin_0
  N17: U1.Q2, R16.Pin_0
  N18: U1.Q3, R18.Pin_0
  N19: U1.Q4, R13.Pin_0
  N20: U1.Q5, R15.Pin_0
  N21: U1.Q6, R12.Pin_0
  N22: U1.Q7, R17.Pin_0
  N23: U1.Q0, R14.Pin_0
  N24: DAC1.VOUT, IC1.no_name_yet#8
  N25: U2.Q1, R3.Pin_0
  N26: U2.Q2, R8.Pin_0
  N27: U2.Q3, R10.Pin_0
  N28: U2.Q4, R7.Pin_0
  N29: U2.Q5, R6.Pin_0
  N30: U2.Q6, R5.Pin_0
  N31: U2.Q7, R9.Pin_0
  N32: U2.Q0, R4.Pin_0
  N33: IC1.no_name_yet#2, R1.Pin_1, LED1.anode
  N34: IC1.no_name_yet#3, LED2.anode, R2.Pin_1
  N35: 7_Segment5.Segment_E, R7.Pin_1
  N36: 7_Segment5.Segment_D, R6.Pin_1
  N37: 7_Segment5.common_cathode, 7_Segment6.common_cathode
  N38: 7_Segment5.Segment_C, R5.Pin_1
  N39: 7_Segment5.Segment_DP, R10.Pin_1
  N40: 7_Segment5.Segment_B, R4.Pin_1
  N41: 7_Segment5.Segment_A, R3.Pin_1
  N42: 7_Segment5.Segment_F, R8.Pin_1
  N43: 7_Segment5.Segment_G, R9.Pin_1
  N44: 7_Segment6.Segment_E, R13.Pin_1
  N45: 7_Segment6.Segment_D, R15.Pin_1
  N46: 7_Segment6.Segment_C, R12.Pin_1
  N47: 7_Segment6.Segment_DP, R18.Pin_1
  N48: 7_Segment6.Segment_B, R14.Pin_1
  N49: 7_Segment6.Segment_A, R11.Pin_1
  N50: 7_Segment6.Segment_F, R16.Pin_1
  N51: 7_Segment6.Segment_G, R17.Pin_1

notes:
  NTE 3079
  7 segment display specs:
  Common Cathode
  U: min 1.6V, typ 1.85V, max 2.4V
  I: 20mA
  Vcc:3.3V => Vr=[0.9;1.7]V
  R = U/I = [0.9;1.7]V/0.02A ~ [45;85] Ohms
  Expecting 20mA is nominal, hence we can use less current to drive the display element.
  Smallest R=180 Ohm, might be too small.
  For Vcc=5V => Vr=[2.6;3.4]V => R=[130;170] Ohms
  NTE 3079 Pin and display configuration
  Coding
  --A--
  F| |B
  --G--
  E| |C
  --D-- *DP
  pin element Qx
  1 E (lower left bar) 0
  2 D (bottom bar) 1
  3 Common Cathode -
  4 C (lower right bar) 2
  5 DP (dot) 3
  6 B (upper right bar) 4
  7 A (top bar) 5
  8 Common Cathode -
  9 F (upper left bar) 6
  10 G (middle bar) 7
  Digit elements on pin sequence
  '0' ABCDEF 11-1011-10
  '1' BC 00-1010-00
  '2' ABDEG 11-0011-01
  '3' ABCDG 01-1011-01
  '4' BCFG 01-1010-11
  '5' ACDFG 01-1001-11
  '6' ACDEFG 11-1001-11
  '7' ABC 00-1011-00
  '8' ABCDEFG 11-1011-11
  '9' ABCDFG 01-1011-11
  '.' DP 00-0100-00
  'A' ABCEFG 10-1011-11
  'B'='8'
  'C' ADEF 11-0001-10
  'D'='0'
  'E' ADEFG 11-0001-11
  'F' AEFG 10-0001-11
  'G' ACDEF 11-1001-10
  'H' BCEFG 10-1010-11
  'I' EF 10-0000-10
  'J' BCD 01-1010-00
  'K'='H'
  'L' DEF 11-0000-10
  'M' ABCEF 10-1011-10
  'N'='H'
  'O'='0'
  'P' ABEFG 10-0011-11
  'Q' ABCFG 00-1011-11
  'R'='A'
  'S'='5'
  'T' DEFG 11-0000-11
  'U' BCDEF 11-1010-10
  'V'='U'
  'W' BCDEFG 11-1010-11
  'X'='H'
  'Y'='4'
  'Z'='2'
  74HC595 vs spec
  DS=SER: Serial Input
  OE=!OE: OutputEnable, active low
  ST_CP=RCLK: Storage Register Clock, +Edge
  SH_CP=SRCLK: Shift Register Clock, +Edge
  MR=!SRCLR: Shift Register CLeaR, active low
  NOTE:
  If ST_CP=SH_CP, Shift Register is always one clock pulse ahead of Storage Register!
  GPIO control for 74HC595
  GPIO14 U2 DS
  GPIO15 U2 ST_CP (latch pulse)
  GPIO16 U2 !OE
  GPIO17 U1 DS
  GPIO18 U1 ST_CP (latch pulse)
  GPIO10 U1 !OE
  Timing:
  1) Write serial data (MSB first) to DS clocked by GPIO4
  2) After eighth bit, generate positive edge on ST_CP to latch data.
  3) Set !OE = 0 to enable display output.
  GPIO control for DAC
  GPIO5 DAC Address selection
  GPIO2 (SDA) I2C Serial Data
  GPIO3 (SCLK) I2C Serial Clock
  GPIO control for ADC
  GPIO10 SPI MOSI->D_IN
  GPIO9 SPI MISO->D_OUT
  GPIO11 SPI CLK
  GPIO8 SPI CE0 N, CS/SHDN

custom parts:
  T Cobbler Plus: The T-Cobbler Plus is an add on prototyping board from Adafruit specifically designed for the Raspberry Pi B+ that can break out all those tasty power, GPIO, I2C and SPI pins from the 40-pin header onto a solderless breadboard. This set will make "cobbling together" prototypes with the Pi super easy. The T-Cobbler Plus can plug into any solderless breadboard.
  MCP4725 12-bit DAC Breakout: MCP4725 12-bit Digital-to-Analog Converter
  7-Segment LED I2C Backpack (red): 4-digit, 7-segment LED Display with I2C Control
